// Logisim project CSE332.6_1921079642_Mosroor_Lab01_Design of a 2-bit Logic unit.circ as structural Verilog: 1 circuit, main circuit main
module main (
  input  A1,
  input  B1,
  input  [1:0] S1_S0,
  input  A0,
  input  B0,
  output F1,
  output F0
);

  wire and_1_out, and_2_out, not_1_out, not_2_out, or_1_out, or_2_out, xor_1_out, xor_2_out;

  and and_1 (and_1_out, A1, B1);
  or or_1 (or_1_out, A1, B1);
  xor xor_1 (xor_1_out, A1, B1);
  not not_1 (not_1_out, A1);
  and and_2 (and_2_out, A0, B0);
  or or_2 (or_2_out, A0, B0);
  xor xor_2 (xor_2_out, A0, B0);
  not not_2 (not_2_out, A0);
  Multiplexer #(.select(2), .enable("false")) multiplexer_1 (
    .in0(and_1_out), .in1(or_1_out), .in2(xor_1_out), .in3(not_1_out), .out(F1), .sel(S1_S0));
  Multiplexer #(.select(2), .enable("false")) multiplexer_2 (
    .in0(and_2_out), .in1(or_2_out), .in2(xor_2_out), .in3(not_2_out), .out(F0), .sel(S1_S0));

  // Notes on the sheet:
  //   1921079642
  //   Mosroor Mofiz Arman
endmodule
