// Logisim project CSE332.6_1921079642_Mosroor_Lab02_Design a 4-bit by 4-bit Binary Multiplication Unit.circ as structural Verilog: 1 circuit, main circuit main
module main (
  input  [3:0] B4_B3_B2_B1,
  input  [3:0] A4_A3_A2_A1,
  output [7:0] out_3
);

  wire [2:0] and_14_out;
  wire [3:0] adder_2_out, and_4_out, and_9_out, and_11_out;
  wire [3:1] adder_3_out;
  wire [3:3] adder_3_cout;

  and and_1 (and_4_out[2], A4_A3_A2_A1[3], B4_B3_B2_B1[2]);
  and and_2 (and_4_out[3], A4_A3_A2_A1[3], B4_B3_B2_B1[3]);
  and and_3 (and_4_out[1], A4_A3_A2_A1[3], B4_B3_B2_B1[1]);
  and and_4 (and_4_out[0], A4_A3_A2_A1[3], B4_B3_B2_B1[0]);
  and and_5 (and_9_out[3], A4_A3_A2_A1[2], B4_B3_B2_B1[3]);
  and and_6 (and_9_out[2], A4_A3_A2_A1[2], B4_B3_B2_B1[2]);
  and and_7 (and_9_out[1], A4_A3_A2_A1[2], B4_B3_B2_B1[1]);
  Adder #(.width(4)) adder_1 (.a(adder_2_out), .b(and_4_out), .out(out_3[6:3]), .cout(out_3[7]));  // open: cin
  and and_8 (and_11_out[3], A4_A3_A2_A1[1], B4_B3_B2_B1[3]);
  and and_9 (and_9_out[0], A4_A3_A2_A1[2], B4_B3_B2_B1[0]);
  and and_10 (and_11_out[2], A4_A3_A2_A1[1], B4_B3_B2_B1[2]);
  and and_11 (and_11_out[0], A4_A3_A2_A1[1], B4_B3_B2_B1[0]);
  and and_12 (and_11_out[1], A4_A3_A2_A1[1], B4_B3_B2_B1[1]);
  Adder #(.width(4)) adder_2 (
    .a({adder_3_cout[3], adder_3_out}), .b(and_9_out), .out({adder_2_out[2:0], out_3[2]}),
    .cout(adder_2_out[3]));  // open: cin
  and and_13 (and_14_out[2], A4_A3_A2_A1[0], B4_B3_B2_B1[3]);
  Adder #(.width(4)) adder_3 (
    .a({1'b0, and_14_out}), .b(and_11_out), .out({adder_3_out, out_3[1]}), .cout(adder_3_cout[3]));  // open: cin
  and and_14 (and_14_out[0], A4_A3_A2_A1[0], B4_B3_B2_B1[1]);
  and and_15 (and_14_out[1], A4_A3_A2_A1[0], B4_B3_B2_B1[2]);
  and and_16 (out_3[0], A4_A3_A2_A1[0], B4_B3_B2_B1[0]);

  // Notes on the sheet:
  //   A4B4
  //   A4B3
  //   A4B1
  //   A4B2
  //   A3B3
  //   A3B4
  //   A3B2
  //   A2B4
  //   A3B1
  //   Mosroor Mofiz Arman 1921079642
  //   A2B3
  //   A2B2
  //   A2B1
  //   A1B3
  //   A1B4
  //   A1B2
  //   A1B1
  //   S8 S7 S6 S5 S4 S3 S2 S1
endmodule
